# Fritzing sketch ART-shield (saved by Fritzing 0.4.3b)

parts:
  MH = Generic female header - 4 pins [package=THT]
  Arduino_Uno = Arduino
  RS = Generic female header - 4 pins [package=THT]
  IR = Generic female header - 6 pins [package=THT]
  US = Generic female header - 10 pins [package=THT]
  RS_2 = Generic female header - 2 pins [package=THT]
  RHF2 = Generic female header - 9 pins
  RFH1 = Generic female header - 9 pins
  CPLD = DIP - 40 pins

nets:
  N1: MH.pin1, CPLD.connector24
  N2: MH.pin2, CPLD.connector23
  N3: MH.pin3, CPLD.connector22
  N4: MH.pin4, CPLD.connector21
  N5: Arduino_Uno.GND, IR.pin5, US.pin9, RFH1.connector0, RFH1.connector1, CPLD.connector20
  N6: Arduino_Uno.D13, RFH1.connector3
  N7: Arduino_Uno.D12, RHF2.connector3
  N8: Arduino_Uno.D11, RFH1.connector2
  N9: Arduino_Uno.D10, RHF2.connector5
  N10: Arduino_Uno.D7, CPLD.connector9
  N11: Arduino_Uno.D6, CPLD.connector8
  N12: Arduino_Uno.D5, CPLD.connector3
  N13: Arduino_Uno.D4, CPLD.connector2
  N14: Arduino_Uno.D3, CPLD.connector1
  N15: Arduino_Uno.D2, CPLD.connector0
  N16: Arduino_Uno.+5V, IR.pin6, US.pin10, RHF2.connector0, CPLD.connector19
  N17: Arduino_Uno.A2, CPLD.connector36
  N18: Arduino_Uno.A3, CPLD.connector37
  N19: Arduino_Uno.A4, CPLD.connector38
  N20: Arduino_Uno.A5, CPLD.connector39
  N21: RS.pin1, CPLD.connector13
  N22: RS.pin2, CPLD.connector12
  N23: RS.pin3, CPLD.connector11
  N24: RS.pin4, CPLD.connector10
  N25: IR.pin1, CPLD.connector14
  N26: IR.pin2, CPLD.connector15
  N27: IR.pin3, CPLD.connector16
  N28: IR.pin4, CPLD.connector17
  N29: US.pin1, CPLD.connector35
  N30: US.pin2, CPLD.connector33
  N31: US.pin3, CPLD.connector32
  N32: US.pin4, CPLD.connector31
  N33: US.pin5, CPLD.connector30
  N34: US.pin6, CPLD.connector29
  N35: US.pin7, CPLD.connector28
  N36: US.pin8, CPLD.connector27
  N37: RS_2.pin1, CPLD.connector26
  N38: RS_2.pin2, CPLD.connector25

notes:
  ART Shield 1
  Ricky Ng-Adam, 2011
