# Fritzing sketch ART (saved by Fritzing 0.4.3b)

parts:
  IC1 = DIP - 40 pins
  RF_transceiver = RFC-1100A
  IF_Header = Generic female header - 3 pins [package=THT]
  UF_Header = Generic female header - 4 pins [package=THT]
  RFH2 = Generic female header - 9 pins [package=THT]
  RFH1 = Generic female header - 9 pins [package=THT]
  Infrared_Forward = Infrared Proximity Sensor
  Arduino1 = Arduino
  IR_Header = Generic female header - 3 pins [package=THT]
  UR_Header = Generic female header - 4 pins [package=THT]
  Infrared_Right = Infrared Proximity Sensor
  Motor_Header = Generic female header - 4 pins [package=THT]
  IB_Header = Generic female header - 3 pins [package=THT]
  UB_Header = Generic female header - 4 pins [package=THT]
  Infrared_Backward = Infrared Proximity Sensor
  IL_Header = Generic female header - 3 pins [package=THT]
  UL_Header = Generic female header - 4 pins [package=THT]
  Infrared_Left = Infrared Proximity Sensor
  Ultrasonic_Forward = SRF05 Ultrasonic Rangefinder
  Ultrasonic_Left = SRF05 Ultrasonic Rangefinder
  Ultrasonic_Right = SRF05 Ultrasonic Rangefinder
  Ultrasonic_Backward = SRF05 Ultrasonic Rangefinder

nets:
  N1: IC1.connector0, Arduino1.D2
  N2: IC1.connector1, Arduino1.D3
  N3: IC1.connector2, Arduino1.D4
  N4: IC1.connector3, Arduino1.D5
  N5: IC1.connector8, Arduino1.D6
  N6: IC1.connector9, Arduino1.D7
  N7: IC1.connector10, UL_Header.pin3, Ultrasonic_Left.connector9
  N8: IC1.connector11, UL_Header.pin2, Ultrasonic_Left.connector10
  N9: IC1.connector12, Arduino1.D8
  N10: IC1.connector13, Arduino1.D9
  N11: IC1.connector15, IL_Header.pin3, Infrared_Left.Vout
  N12: IC1.connector16, IB_Header.pin3, Infrared_Backward.Vout
  N13: IC1.connector21, Motor_Header.pin4
  N14: IC1.connector22, Motor_Header.pin3
  N15: IC1.connector23, Motor_Header.pin2
  N16: IC1.connector24, Motor_Header.pin1
  N17: IC1.connector25, UB_Header.pin3, Ultrasonic_Backward.connector9
  N18: IC1.connector26, UB_Header.pin2, Ultrasonic_Backward.connector10
  N19: IC1.connector27, IR_Header.pin3, Infrared_Right.Vout
  N20: IC1.connector31, UR_Header.pin3, Ultrasonic_Right.connector9
  N21: IC1.connector32, UR_Header.pin2, Ultrasonic_Right.connector10
  N22: IC1.connector33, IF_Header.pin3, Infrared_Forward.Vout
  N23: IC1.connector35, UF_Header.pin2, Ultrasonic_Forward.connector10
  N24: IC1.connector36, UF_Header.pin3, Ultrasonic_Forward.connector9
  N25: IC1.connector37, Arduino1.A1
  N26: IC1.connector38, Arduino1.A2
  N27: IC1.connector39, Arduino1.A3
  VCC: RF_transceiver.connector0, IF_Header.pin1, UF_Header.pin4, RFH2.pin9, RFH1.pin1, RFH1.pin2, Infrared_Forward.Vcc, Arduino1.+5V, IR_Header.pin1, UR_Header.pin4, Infrared_Right.Vcc, IL_Header.pin1, UL_Header.pin4, Infrared_Left.Vcc, Ultrasonic_Forward.connector8, Ultrasonic_Left.connector8, Ultrasonic_Right.connector8
  N28: RF_transceiver.connector3, RFH1.pin4, RFH1.pin5, Arduino1.D12
  N29: RF_transceiver.connector5, RFH1.pin6, RFH1.pin7, Arduino1.D13
  N30: RF_transceiver.connector14, RFH2.pin4, RFH2.pin5, Arduino1.D10
  N31: RF_transceiver.connector15, RFH2.pin3, Arduino1.D11
  GND: RF_transceiver.connector17, IF_Header.pin2, UF_Header.pin1, RFH2.pin1, RFH2.pin2, Infrared_Forward.GND, Arduino1.GND, IR_Header.pin2, UR_Header.pin1, Infrared_Right.GND, IB_Header.pin2, Infrared_Backward.GND, IL_Header.pin2, UL_Header.pin1, Infrared_Left.GND, Ultrasonic_Forward.connector11, Ultrasonic_Left.connector11, Ultrasonic_Right.connector11
  N32: IB_Header.pin1, Infrared_Backward.Vcc
  N33: UB_Header.pin1, Ultrasonic_Backward.connector11
  N34: UB_Header.pin4, Ultrasonic_Backward.connector8
